# Fritzing sketch Automatic_Switch_Bedroom (saved by Fritzing 1.0.1rc)

parts:
  Conversor_AC-DC_5V_1000_mA = WX-DC12003 [package=THT]
  Cable_Tipo_C = USB-C plug
  Modulo_Relevador_4_canales_5V = Module 4 Relais 5V [package="Module 4 Relais 5V"]
  OUTPUTS = Terminal 2pin
  TRM2 = Terminal 2pin
  TRM3 = Terminal 2pin
  TRM4 = Terminal 2pin
  INPUT = Terminal 2pin
  ESP32_C3 = Adafruit QT Py ESP32-C3 rev A
  U1 = SWITCH_SPDT [package=kps-1290]
  U2 = SWITCH_SPDT [package=kps-1290]
  U3 = SWITCH_SPDT [package=kps-1290]
  Switches = SWITCH_SPDT [package=kps-1290]
  R2 = Resistor [tolerance=±5% power=0.25W resistance=220 package=THT]
  R3 = Resistor [tolerance=±5% power=0.25W resistance=220 package=THT]
  Resistencias = Resistor [tolerance=±5% power=0.25W resistance=220 package=THT]
  R4 = Resistor [tolerance=±5% power=0.25W resistance=220 package=THT]

nets:
  N1: Conversor_AC-DC_5V_1000_mA.IN-L, Modulo_Relevador_4_canales_5V.K1-NF, Modulo_Relevador_4_canales_5V.K2-NF, Modulo_Relevador_4_canales_5V.K3-NF, Modulo_Relevador_4_canales_5V.K4-NF, INPUT.pin_2
  N2: Conversor_AC-DC_5V_1000_mA.IN-N, OUTPUTS.pin_1, TRM2.pin_1, TRM3.pin_1, TRM4.pin_1, INPUT.pin_1
  N3: Conversor_AC-DC_5V_1000_mA.DC_OUT+, Cable_Tipo_C.VCC
  N4: Conversor_AC-DC_5V_1000_mA.DC_OUT-, Cable_Tipo_C.GND
  VCC: Modulo_Relevador_4_canales_5V.VCC, ESP32_C3.+5V
  GND: Modulo_Relevador_4_canales_5V.GND, ESP32_C3.GND, R2.Pin_1, R3.Pin_1, Resistencias.Pin_1, R4.Pin_1
  N5: Modulo_Relevador_4_canales_5V.IN1, ESP32_C3.A0
  N6: Modulo_Relevador_4_canales_5V.IN2, ESP32_C3.A1
  N7: Modulo_Relevador_4_canales_5V.IN3, ESP32_C3.A2
  N8: Modulo_Relevador_4_canales_5V.IN4, ESP32_C3.A3
  N9: Modulo_Relevador_4_canales_5V.K1-NO, OUTPUTS.pin_2
  N10: Modulo_Relevador_4_canales_5V.K2-NO, TRM2.pin_2
  N11: Modulo_Relevador_4_canales_5V.K3-NO, TRM3.pin_2
  N12: Modulo_Relevador_4_canales_5V.K4-NO, TRM4.pin_2
  N13: ESP32_C3.SDA, U1.S, Resistencias.Pin_0
  N14: ESP32_C3.SCL, U2.S, R2.Pin_0
  N15: ESP32_C3.MISO, U3.S
  N16: ESP32_C3.MOSI, Switches.S, R3.Pin_0
  N17: ESP32_C3.3.3V, U1.P, U2.P, U3.P, Switches.P

notes:
  Automatic Switch
  Amaro, A.
  21/11/2023

custom parts:
  WX-DC12003: Ac to DC power supply 110/220V in 5v 700ma or 12 V 300ma out.
  USB-C plug: power plug
  Module 4 Relais 5V: Module 4 Relais 5V 4x SPD-06VDC-SD-C
  Terminal 2pin: 2-pin Terminal Block
